// Logisim project alu16.circ as structural Verilog: 2 circuits, main circuit main
module main (
  input  [15:0] x,
  input  [15:0] _0,
  input  zx,
  input  nx,
  input  te,
  input  [15:0] y,
  input  no,
  input  [15:0] _0_2,
  input  zy,
  input  ny,
  input  f,
  output [15:0] out_12,
  output ts
);

  wire [15:0] adder_1_out, and_1_out, multiplexer_1_out, multiplexer_2_out, multiplexer_3_out,
       multiplexer_4_out, multiplexer_5_out, not_1_out, not_2_out, not_3_out;

  Multiplexer #(.width(16)) multiplexer_1 (.in0(x), .in1(_0), .out(multiplexer_1_out), .sel(zx));  // open: en
  Multiplexer #(.width(16)) multiplexer_2 (.in0(y), .in1(_0_2), .out(multiplexer_2_out), .sel(zy));  // open: en
  assign not_1_out = ~multiplexer_1_out;  // NOT_Gate not_1, 16 bits wide
  assign not_2_out = ~multiplexer_2_out;  // NOT_Gate not_2, 16 bits wide
  Multiplexer #(.width(16)) multiplexer_3 (
    .in0(multiplexer_1_out), .in1(not_1_out), .out(multiplexer_3_out), .sel(nx));  // open: en
  Multiplexer #(.width(16)) multiplexer_4 (
    .in0(multiplexer_2_out), .in1(not_2_out), .out(multiplexer_4_out), .sel(ny));  // open: en
  Adder #(.width(16)) adder_1 (.a(multiplexer_3_out), .b(multiplexer_4_out), .out(adder_1_out), .cin(te), .cout(ts));
  assign and_1_out = multiplexer_3_out & multiplexer_4_out;  // AND_Gate and_1, 16 bits wide
  Multiplexer #(.width(16)) multiplexer_5 (
    .in0(and_1_out), .in1(adder_1_out), .out(multiplexer_5_out), .sel(f));  // open: en
  assign not_3_out = ~multiplexer_5_out;  // NOT_Gate not_3, 16 bits wide
  Multiplexer #(.width(16)) multiplexer_6 (
    .in0(multiplexer_5_out), .in1(not_3_out), .out(out_12), .sel(no));  // open: en
endmodule

module alu16bits (
  input  [15:0] X,
  input  [15:0] _0,
  input  [15:0] Y,
  input  te,
  input  [15:0] _0_2,
  input  no,
  input  zx,
  input  f,
  input  zy,
  input  ny,
  input  nx,
  output [15:0] out_12,
  output ts
);

  main main_1 (
    .x(X), ._0(_0), .y(Y), ._0_2(_0_2), .zx(zx), .zy(zy), .nx(nx), .ny(ny), .f(f), .no(no), .out_12(out_12),
    .te(te), .ts(ts));
endmodule
