// Logisim project alu16bits.circ as structural Verilog: 1 circuit, main circuit main
module main (
  input  x,
  input  _0,
  input  zx,
  input  nx,
  input  te,
  input  y,
  input  no,
  input  _0_2,
  input  zy,
  input  ny,
  input  f,
  output out_12,
  output ts
);

  wire adder_1_out, and_1_out, multiplexer_1_out, multiplexer_2_out, multiplexer_3_out, multiplexer_4_out,
       multiplexer_5_out, not_1_out, not_2_out, not_3_out;

  Multiplexer multiplexer_1 (.in0(x), .in1(_0), .out(multiplexer_1_out), .sel(zx));  // open: en
  Multiplexer multiplexer_2 (.in0(y), .in1(_0_2), .out(multiplexer_2_out), .sel(zy));  // open: en
  not not_1 (not_1_out, multiplexer_1_out);
  not not_2 (not_2_out, multiplexer_2_out);
  Multiplexer multiplexer_3 (.in0(multiplexer_1_out), .in1(not_1_out), .out(multiplexer_3_out), .sel(nx));  // open: en
  Multiplexer multiplexer_4 (.in0(multiplexer_2_out), .in1(not_2_out), .out(multiplexer_4_out), .sel(ny));  // open: en
  Adder #(.width(1)) adder_1 (.a(multiplexer_3_out), .b(multiplexer_4_out), .out(adder_1_out), .cin(te), .cout(ts));
  and and_1 (and_1_out, multiplexer_3_out, multiplexer_4_out);
  Multiplexer multiplexer_5 (.in0(and_1_out), .in1(adder_1_out), .out(multiplexer_5_out), .sel(f));  // open: en
  not not_3 (not_3_out, multiplexer_5_out);
  Multiplexer multiplexer_6 (.in0(multiplexer_5_out), .in1(not_3_out), .out(out_12), .sel(no));  // open: en
endmodule
