// Logisim project bit.circ as structural Verilog: 1 circuit, main circuit main
module main (
  input  in,
  input  load,
  output out
);

  wire clock_1_out, multiplexer_1_out;

  Multiplexer multiplexer_1 (.in0(out), .in1(in), .out(multiplexer_1_out), .sel(load));  // open: en
  Clock clock_1 (.out(clock_1_out));
  Register #(.width(1)) register_1 (.D(multiplexer_1_out), .Q(out), .clk(clock_1_out));  // open: en, clr
endmodule
