// Logisim project trab2.circ as structural Verilog: 8 circuits, main circuit main
module main (
  input  in,
  input  load,
  output out
);

  wire clock_1_out, multiplexer_1_out;

  Multiplexer multiplexer_1 (.in0(out), .in1(in), .out(multiplexer_1_out), .sel(load));  // open: en
  Clock clock_1 (.out(clock_1_out));
  Register #(.width(1)) register_1 (.D(multiplexer_1_out), .Q(out), .clk(clock_1_out));  // open: en, clr
endmodule

module \bit  (
  input  in,
  input  load,
  output out
);

  wire clock_1_out, multiplexer_1_out;

  Multiplexer multiplexer_1 (.in0(out), .in1(in), .out(multiplexer_1_out), .sel(load));  // open: en
  Register #(.width(1)) register_1 (.D(multiplexer_1_out), .Q(out), .clk(clock_1_out));  // open: en, clr
  Clock clock_1 (.out(clock_1_out));
endmodule

module _16bit (
  input  a0,
  input  a1,
  input  a2,
  input  a3,
  input  a4,
  input  a5,
  input  a6,
  input  a7,
  input  a8,
  input  a9,
  input  a10,
  input  a11,
  input  a12,
  input  a13,
  input  a14,
  input  a15,
  input  load,
  output out_18,
  output out_19,
  output out_20,
  output out_21,
  output out_22,
  output out_23,
  output out_24,
  output out_25,
  output out_26,
  output out_27,
  output out_28,
  output out_29,
  output out_30,
  output out_31,
  output out_32,
  output out_33
);

  Clock clock_1 ();  // open: out
  \bit  bit_1 (.in(a0), .load(load), .out(out_18));
  \bit  bit_2 (.in(a1), .load(load), .out(out_19));
  \bit  bit_3 (.in(a2), .load(load), .out(out_20));
  \bit  bit_4 (.in(a3), .load(load), .out(out_21));
  \bit  bit_5 (.in(a4), .load(load), .out(out_22));
  \bit  bit_6 (.in(a5), .load(load), .out(out_23));
  \bit  bit_7 (.in(a6), .load(load), .out(out_24));
  \bit  bit_8 (.in(a7), .load(load), .out(out_25));
  \bit  bit_9 (.in(a8), .load(load), .out(out_26));
  \bit  bit_10 (.in(a9), .load(load), .out(out_27));
  \bit  bit_11 (.in(a10), .load(load), .out(out_28));
  \bit  bit_12 (.in(a11), .load(load), .out(out_29));
  \bit  bit_13 (.in(a12), .load(load), .out(out_30));
  \bit  bit_14 (.in(a13), .load(load), .out(out_31));
  \bit  bit_15 (.in(a14), .load(load), .out(out_32));
  \bit  bit_16 (.in(a15), .load(load), .out(out_33));
endmodule

module RAM8 (
  input  load,
  input  [15:0] in,
  input  [2:0] adress,
  output [15:0] out
);

  wire demultiplexer_2_out0, demultiplexer_2_out1, demultiplexer_2_out2, demultiplexer_2_out3,
       demultiplexer_2_out4, demultiplexer_2_out5, demultiplexer_2_out6, demultiplexer_2_out7;
  wire [15:0] demultiplexer_1_out0, demultiplexer_1_out1, demultiplexer_1_out2, demultiplexer_1_out3,
       demultiplexer_1_out4, demultiplexer_1_out5, demultiplexer_1_out6, demultiplexer_1_out7,
       n16bit_1_out_18, n16bit_2_out_18, n16bit_3_out_18, n16bit_4_out_18, n16bit_5_out_18, n16bit_6_out_18,
       n16bit_7_out_18, n16bit_8_out_18;

  Clock clock_1 ();  // open: out
  Demultiplexer #(.select(3), .width(16)) demultiplexer_1 (
    .out0(demultiplexer_1_out0), .out1(demultiplexer_1_out1), .out2(demultiplexer_1_out2),
    .out3(demultiplexer_1_out3), .out4(demultiplexer_1_out4), .out5(demultiplexer_1_out5),
    .out6(demultiplexer_1_out6), .out7(demultiplexer_1_out7), .in(in), .sel(adress));  // open: en
  Demultiplexer #(.select(3)) demultiplexer_2 (
    .out0(demultiplexer_2_out0), .out1(demultiplexer_2_out1), .out2(demultiplexer_2_out2),
    .out3(demultiplexer_2_out3), .out4(demultiplexer_2_out4), .out5(demultiplexer_2_out5),
    .out6(demultiplexer_2_out6), .out7(demultiplexer_2_out7), .in(load), .sel(adress));  // open: en
  _16bit u_16bit_1 (
    .a0(demultiplexer_1_out0[0]), .a1(demultiplexer_1_out0[1]), .a2(demultiplexer_1_out0[2]),
    .a3(demultiplexer_1_out0[3]), .a4(demultiplexer_1_out0[4]), .a5(demultiplexer_1_out0[5]),
    .a6(demultiplexer_1_out0[6]), .a7(demultiplexer_1_out0[7]), .a8(demultiplexer_1_out0[8]),
    .a9(demultiplexer_1_out0[9]), .a10(demultiplexer_1_out0[10]), .a11(demultiplexer_1_out0[11]),
    .a12(demultiplexer_1_out0[12]), .a13(demultiplexer_1_out0[13]), .a14(demultiplexer_1_out0[14]),
    .a15(demultiplexer_1_out0[15]), .load(demultiplexer_2_out0), .out_18(n16bit_1_out_18[0]),
    .out_19(n16bit_1_out_18[1]), .out_20(n16bit_1_out_18[2]), .out_21(n16bit_1_out_18[3]),
    .out_22(n16bit_1_out_18[4]), .out_23(n16bit_1_out_18[5]), .out_24(n16bit_1_out_18[6]),
    .out_25(n16bit_1_out_18[7]), .out_26(n16bit_1_out_18[8]), .out_27(n16bit_1_out_18[9]),
    .out_28(n16bit_1_out_18[10]), .out_29(n16bit_1_out_18[11]), .out_30(n16bit_1_out_18[12]),
    .out_31(n16bit_1_out_18[13]), .out_32(n16bit_1_out_18[14]), .out_33(n16bit_1_out_18[15]));
  _16bit u_16bit_2 (
    .a0(demultiplexer_1_out1[0]), .a1(demultiplexer_1_out1[1]), .a2(demultiplexer_1_out1[2]),
    .a3(demultiplexer_1_out1[3]), .a4(demultiplexer_1_out1[4]), .a5(demultiplexer_1_out1[5]),
    .a6(demultiplexer_1_out1[6]), .a7(demultiplexer_1_out1[7]), .a8(demultiplexer_1_out1[8]),
    .a9(demultiplexer_1_out1[9]), .a10(demultiplexer_1_out1[10]), .a11(demultiplexer_1_out1[11]),
    .a12(demultiplexer_1_out1[12]), .a13(demultiplexer_1_out1[13]), .a14(demultiplexer_1_out1[14]),
    .a15(demultiplexer_1_out1[15]), .load(demultiplexer_2_out1), .out_18(n16bit_2_out_18[0]),
    .out_19(n16bit_2_out_18[1]), .out_20(n16bit_2_out_18[2]), .out_21(n16bit_2_out_18[3]),
    .out_22(n16bit_2_out_18[4]), .out_23(n16bit_2_out_18[5]), .out_24(n16bit_2_out_18[6]),
    .out_25(n16bit_2_out_18[7]), .out_26(n16bit_2_out_18[8]), .out_27(n16bit_2_out_18[9]),
    .out_28(n16bit_2_out_18[10]), .out_29(n16bit_2_out_18[11]), .out_30(n16bit_2_out_18[12]),
    .out_31(n16bit_2_out_18[13]), .out_32(n16bit_2_out_18[14]), .out_33(n16bit_2_out_18[15]));
  _16bit u_16bit_3 (
    .a0(demultiplexer_1_out2[0]), .a1(demultiplexer_1_out2[1]), .a2(demultiplexer_1_out2[2]),
    .a3(demultiplexer_1_out2[3]), .a4(demultiplexer_1_out2[4]), .a5(demultiplexer_1_out2[5]),
    .a6(demultiplexer_1_out2[6]), .a7(demultiplexer_1_out2[7]), .a8(demultiplexer_1_out2[8]),
    .a9(demultiplexer_1_out2[9]), .a10(demultiplexer_1_out2[10]), .a11(demultiplexer_1_out2[11]),
    .a12(demultiplexer_1_out2[12]), .a13(demultiplexer_1_out2[13]), .a14(demultiplexer_1_out2[14]),
    .a15(demultiplexer_1_out2[15]), .load(demultiplexer_2_out2), .out_18(n16bit_3_out_18[0]),
    .out_19(n16bit_3_out_18[1]), .out_20(n16bit_3_out_18[2]), .out_21(n16bit_3_out_18[3]),
    .out_22(n16bit_3_out_18[4]), .out_23(n16bit_3_out_18[5]), .out_24(n16bit_3_out_18[6]),
    .out_25(n16bit_3_out_18[7]), .out_26(n16bit_3_out_18[8]), .out_27(n16bit_3_out_18[9]),
    .out_28(n16bit_3_out_18[10]), .out_29(n16bit_3_out_18[11]), .out_30(n16bit_3_out_18[12]),
    .out_31(n16bit_3_out_18[13]), .out_32(n16bit_3_out_18[14]), .out_33(n16bit_3_out_18[15]));
  _16bit u_16bit_4 (
    .a0(demultiplexer_1_out3[0]), .a1(demultiplexer_1_out3[1]), .a2(demultiplexer_1_out3[2]),
    .a3(demultiplexer_1_out3[3]), .a4(demultiplexer_1_out3[4]), .a5(demultiplexer_1_out3[5]),
    .a6(demultiplexer_1_out3[6]), .a7(demultiplexer_1_out3[7]), .a8(demultiplexer_1_out3[8]),
    .a9(demultiplexer_1_out3[9]), .a10(demultiplexer_1_out3[10]), .a11(demultiplexer_1_out3[11]),
    .a12(demultiplexer_1_out3[12]), .a13(demultiplexer_1_out3[13]), .a14(demultiplexer_1_out3[14]),
    .a15(demultiplexer_1_out3[15]), .load(demultiplexer_2_out3), .out_18(n16bit_4_out_18[0]),
    .out_19(n16bit_4_out_18[1]), .out_20(n16bit_4_out_18[2]), .out_21(n16bit_4_out_18[3]),
    .out_22(n16bit_4_out_18[4]), .out_23(n16bit_4_out_18[5]), .out_24(n16bit_4_out_18[6]),
    .out_25(n16bit_4_out_18[7]), .out_26(n16bit_4_out_18[8]), .out_27(n16bit_4_out_18[9]),
    .out_28(n16bit_4_out_18[10]), .out_29(n16bit_4_out_18[11]), .out_30(n16bit_4_out_18[12]),
    .out_31(n16bit_4_out_18[13]), .out_32(n16bit_4_out_18[14]), .out_33(n16bit_4_out_18[15]));
  _16bit u_16bit_5 (
    .a0(demultiplexer_1_out4[0]), .a1(demultiplexer_1_out4[1]), .a2(demultiplexer_1_out4[2]),
    .a3(demultiplexer_1_out4[3]), .a4(demultiplexer_1_out4[4]), .a5(demultiplexer_1_out4[5]),
    .a6(demultiplexer_1_out4[6]), .a7(demultiplexer_1_out4[7]), .a8(demultiplexer_1_out4[8]),
    .a9(demultiplexer_1_out4[9]), .a10(demultiplexer_1_out4[10]), .a11(demultiplexer_1_out4[11]),
    .a12(demultiplexer_1_out4[12]), .a13(demultiplexer_1_out4[13]), .a14(demultiplexer_1_out4[14]),
    .a15(demultiplexer_1_out4[15]), .load(demultiplexer_2_out4), .out_18(n16bit_5_out_18[0]),
    .out_19(n16bit_5_out_18[1]), .out_20(n16bit_5_out_18[2]), .out_21(n16bit_5_out_18[3]),
    .out_22(n16bit_5_out_18[4]), .out_23(n16bit_5_out_18[5]), .out_24(n16bit_5_out_18[6]),
    .out_25(n16bit_5_out_18[7]), .out_26(n16bit_5_out_18[8]), .out_27(n16bit_5_out_18[9]),
    .out_28(n16bit_5_out_18[10]), .out_29(n16bit_5_out_18[11]), .out_30(n16bit_5_out_18[12]),
    .out_31(n16bit_5_out_18[13]), .out_32(n16bit_5_out_18[14]), .out_33(n16bit_5_out_18[15]));
  _16bit u_16bit_6 (
    .a0(demultiplexer_1_out5[0]), .a1(demultiplexer_1_out5[1]), .a2(demultiplexer_1_out5[2]),
    .a3(demultiplexer_1_out5[3]), .a4(demultiplexer_1_out5[4]), .a5(demultiplexer_1_out5[5]),
    .a6(demultiplexer_1_out5[6]), .a7(demultiplexer_1_out5[7]), .a8(demultiplexer_1_out5[8]),
    .a9(demultiplexer_1_out5[9]), .a10(demultiplexer_1_out5[10]), .a11(demultiplexer_1_out5[11]),
    .a12(demultiplexer_1_out5[12]), .a13(demultiplexer_1_out5[13]), .a14(demultiplexer_1_out5[14]),
    .a15(demultiplexer_1_out5[15]), .load(demultiplexer_2_out5), .out_18(n16bit_6_out_18[0]),
    .out_19(n16bit_6_out_18[1]), .out_20(n16bit_6_out_18[2]), .out_21(n16bit_6_out_18[3]),
    .out_22(n16bit_6_out_18[4]), .out_23(n16bit_6_out_18[5]), .out_24(n16bit_6_out_18[6]),
    .out_25(n16bit_6_out_18[7]), .out_26(n16bit_6_out_18[8]), .out_27(n16bit_6_out_18[9]),
    .out_28(n16bit_6_out_18[10]), .out_29(n16bit_6_out_18[11]), .out_30(n16bit_6_out_18[12]),
    .out_31(n16bit_6_out_18[13]), .out_32(n16bit_6_out_18[14]), .out_33(n16bit_6_out_18[15]));
  _16bit u_16bit_7 (
    .a0(demultiplexer_1_out6[0]), .a1(demultiplexer_1_out6[1]), .a2(demultiplexer_1_out6[2]),
    .a3(demultiplexer_1_out6[3]), .a4(demultiplexer_1_out6[4]), .a5(demultiplexer_1_out6[5]),
    .a6(demultiplexer_1_out6[6]), .a7(demultiplexer_1_out6[7]), .a8(demultiplexer_1_out6[8]),
    .a9(demultiplexer_1_out6[9]), .a10(demultiplexer_1_out6[10]), .a11(demultiplexer_1_out6[11]),
    .a12(demultiplexer_1_out6[12]), .a13(demultiplexer_1_out6[13]), .a14(demultiplexer_1_out6[14]),
    .a15(demultiplexer_1_out6[15]), .load(demultiplexer_2_out6), .out_18(n16bit_7_out_18[0]),
    .out_19(n16bit_7_out_18[1]), .out_20(n16bit_7_out_18[2]), .out_21(n16bit_7_out_18[3]),
    .out_22(n16bit_7_out_18[4]), .out_23(n16bit_7_out_18[5]), .out_24(n16bit_7_out_18[6]),
    .out_25(n16bit_7_out_18[7]), .out_26(n16bit_7_out_18[8]), .out_27(n16bit_7_out_18[9]),
    .out_28(n16bit_7_out_18[10]), .out_29(n16bit_7_out_18[11]), .out_30(n16bit_7_out_18[12]),
    .out_31(n16bit_7_out_18[13]), .out_32(n16bit_7_out_18[14]), .out_33(n16bit_7_out_18[15]));
  _16bit u_16bit_8 (
    .a0(demultiplexer_1_out7[0]), .a1(demultiplexer_1_out7[1]), .a2(demultiplexer_1_out7[2]),
    .a3(demultiplexer_1_out7[3]), .a4(demultiplexer_1_out7[4]), .a5(demultiplexer_1_out7[5]),
    .a6(demultiplexer_1_out7[6]), .a7(demultiplexer_1_out7[7]), .a8(demultiplexer_1_out7[8]),
    .a9(demultiplexer_1_out7[9]), .a10(demultiplexer_1_out7[10]), .a11(demultiplexer_1_out7[11]),
    .a12(demultiplexer_1_out7[12]), .a13(demultiplexer_1_out7[13]), .a14(demultiplexer_1_out7[14]),
    .a15(demultiplexer_1_out7[15]), .load(demultiplexer_2_out7), .out_18(n16bit_8_out_18[0]),
    .out_19(n16bit_8_out_18[1]), .out_20(n16bit_8_out_18[2]), .out_21(n16bit_8_out_18[3]),
    .out_22(n16bit_8_out_18[4]), .out_23(n16bit_8_out_18[5]), .out_24(n16bit_8_out_18[6]),
    .out_25(n16bit_8_out_18[7]), .out_26(n16bit_8_out_18[8]), .out_27(n16bit_8_out_18[9]),
    .out_28(n16bit_8_out_18[10]), .out_29(n16bit_8_out_18[11]), .out_30(n16bit_8_out_18[12]),
    .out_31(n16bit_8_out_18[13]), .out_32(n16bit_8_out_18[14]), .out_33(n16bit_8_out_18[15]));
  Multiplexer #(.select(3), .width(16)) multiplexer_1 (
    .in0(n16bit_1_out_18), .in1(n16bit_2_out_18), .in2(n16bit_3_out_18), .in3(n16bit_4_out_18),
    .in4(n16bit_5_out_18), .in5(n16bit_6_out_18), .in6(n16bit_7_out_18), .in7(n16bit_8_out_18), .out(out),
    .sel(adress));  // open: en
endmodule

module RAM64 (
  input  [2:0] adress,
  input  [2:0] adress_2,
  input  [15:0] in,
  output [15:0] out
);

  wire demultiplexer_1_out0, demultiplexer_1_out1, demultiplexer_1_out2, demultiplexer_1_out3,
       demultiplexer_1_out4, demultiplexer_1_out5, demultiplexer_1_out6, demultiplexer_1_out7;
  wire [15:0] ram8_1_out, ram8_2_out, ram8_3_out, ram8_4_out, ram8_5_out, ram8_6_out, ram8_7_out, ram8_8_out;

  Clock clock_1 ();  // open: out
  Demultiplexer #(.select(3)) demultiplexer_1 (
    .out0(demultiplexer_1_out0), .out1(demultiplexer_1_out1), .out2(demultiplexer_1_out2),
    .out3(demultiplexer_1_out3), .out4(demultiplexer_1_out4), .out5(demultiplexer_1_out5),
    .out6(demultiplexer_1_out6), .out7(demultiplexer_1_out7), .sel(adress));  // open: in, en
  RAM #(.addrWidth(6), .dataWidth(16)) ram_1 ();  // open: addr, data, sel, clk, ld, clr
  RAM8 ram8_1 (.in(in), .adress(adress_2), .load(demultiplexer_1_out0), .out(ram8_1_out));
  RAM8 ram8_2 (.in(in), .adress(adress_2), .load(demultiplexer_1_out1), .out(ram8_2_out));
  RAM8 ram8_3 (.in(in), .adress(adress_2), .load(demultiplexer_1_out2), .out(ram8_3_out));
  RAM8 ram8_4 (.in(in), .adress(adress_2), .load(demultiplexer_1_out3), .out(ram8_4_out));
  RAM8 ram8_5 (.in(in), .adress(adress_2), .load(demultiplexer_1_out4), .out(ram8_5_out));
  RAM8 ram8_6 (.in(in), .adress(adress_2), .load(demultiplexer_1_out5), .out(ram8_6_out));
  RAM8 ram8_7 (.in(in), .adress(adress_2), .load(demultiplexer_1_out6), .out(ram8_7_out));
  RAM8 ram8_8 (.in(in), .adress(adress_2), .load(demultiplexer_1_out7), .out(ram8_8_out));
  Multiplexer #(.select(3), .width(16)) multiplexer_1 (
    .in0(ram8_1_out), .in1(ram8_2_out), .in2(ram8_3_out), .in3(ram8_4_out), .in4(ram8_5_out),
    .in5(ram8_6_out), .in6(ram8_7_out), .in7(ram8_8_out), .out(out), .sel(adress));  // open: en
endmodule

module RAM512 (
  input  [5:0] adress,
  input  [2:0] adress_dumu,
  input  load,
  input  [15:0] in,
  output [15:0] out
);

  wire clock_1_out, demultiplexer_1_out0, demultiplexer_1_out1, demultiplexer_1_out2, demultiplexer_1_out3,
       demultiplexer_1_out4, demultiplexer_1_out5, demultiplexer_1_out6, demultiplexer_1_out7;
  wire [15:0] ram_1_data, ram_2_data, ram_3_data, ram_4_data, ram_5_data, ram_6_data, ram_7_data, ram_8_data;

  Demultiplexer #(.select(3)) demultiplexer_1 (
    .out0(demultiplexer_1_out0), .out1(demultiplexer_1_out1), .out2(demultiplexer_1_out2),
    .out3(demultiplexer_1_out3), .out4(demultiplexer_1_out4), .out5(demultiplexer_1_out5),
    .out6(demultiplexer_1_out6), .out7(demultiplexer_1_out7), .in(load), .sel(adress_dumu));  // open: en
  RAM #(.addrWidth(6), .dataWidth(16), .bus("separate")) ram_1 (
    .addr(adress), .din(in), .data(ram_1_data), .str(demultiplexer_1_out0), .clk(clock_1_out), .ld(1'b1));  // open: sel, clr
  RAM #(.addrWidth(6), .dataWidth(16), .bus("separate")) ram_2 (
    .addr(adress), .din(in), .data(ram_2_data), .str(demultiplexer_1_out1), .clk(clock_1_out), .ld(1'b1));  // open: sel, clr
  RAM #(.addrWidth(6), .dataWidth(16), .bus("separate")) ram_3 (
    .addr(adress), .din(in), .data(ram_3_data), .str(demultiplexer_1_out2), .clk(clock_1_out), .ld(1'b1));  // open: sel, clr
  RAM #(.addrWidth(6), .dataWidth(16), .bus("separate")) ram_4 (
    .addr(adress), .din(in), .data(ram_4_data), .str(demultiplexer_1_out3), .clk(clock_1_out), .ld(1'b1));  // open: sel, clr
  RAM #(.addrWidth(6), .dataWidth(16), .bus("separate")) ram_5 (
    .addr(adress), .din(in), .data(ram_5_data), .str(demultiplexer_1_out4), .clk(clock_1_out), .ld(1'b1));  // open: sel, clr
  RAM #(.addrWidth(6), .dataWidth(16), .bus("separate")) ram_6 (
    .addr(adress), .din(in), .data(ram_6_data), .str(demultiplexer_1_out5), .clk(clock_1_out), .ld(1'b1));  // open: sel, clr
  RAM #(.addrWidth(6), .dataWidth(16), .bus("separate")) ram_7 (
    .addr(adress), .din(in), .data(ram_7_data), .str(demultiplexer_1_out6), .clk(clock_1_out), .ld(1'b1));  // open: sel, clr
  RAM #(.addrWidth(6), .dataWidth(16), .bus("separate")) ram_8 (
    .addr(adress), .din(in), .data(ram_8_data), .str(demultiplexer_1_out7), .clk(clock_1_out), .ld(1'b1));  // open: sel, clr
  Clock clock_1 (.out(clock_1_out));
  Multiplexer #(.select(3), .width(16)) multiplexer_1 (
    .in0(ram_1_data), .in1(ram_2_data), .in2(ram_3_data), .in3(ram_4_data), .in4(ram_5_data),
    .in5(ram_6_data), .in6(ram_7_data), .in7(ram_8_data), .out(out), .sel(adress_dumu));  // open: en
endmodule

module RAM4k (
  input  [2:0] ad_dumu3,
  input  [2:0] ad_dumu2,
  input  [5:0] adress_1,
  input  load,
  input  [15:0] in,
  output [15:0] out
);

  wire demultiplexer_1_out0, demultiplexer_1_out1, demultiplexer_1_out3, demultiplexer_1_out4,
       demultiplexer_1_out5, demultiplexer_1_out6, demultiplexer_1_out7;
  wire [15:0] ram512_1_out, ram512_2_out, ram512_3_out, ram512_4_out, ram512_5_out, ram512_6_out,
       ram512_7_out, ram512_8_out;

  Clock clock_1 ();  // open: out
  Demultiplexer #(.select(3)) demultiplexer_1 (
    .out0(demultiplexer_1_out0), .out1(demultiplexer_1_out1), .out2(demultiplexer_1_out1),
    .out3(demultiplexer_1_out3), .out4(demultiplexer_1_out4), .out5(demultiplexer_1_out5),
    .out6(demultiplexer_1_out6), .out7(demultiplexer_1_out7), .in(load), .sel(ad_dumu3));  // open: en
  RAM512 ram512_1 (.adress(adress_1), .adress_dumu(ad_dumu2), .load(demultiplexer_1_out0), .in(in), .out(ram512_1_out));
  RAM512 ram512_2 (.adress(adress_1), .adress_dumu(ad_dumu2), .load(demultiplexer_1_out1), .in(in), .out(ram512_2_out));
  RAM512 ram512_3 (.adress(adress_1), .adress_dumu(ad_dumu2), .load(demultiplexer_1_out1), .in(in), .out(ram512_3_out));
  RAM512 ram512_4 (.adress(adress_1), .adress_dumu(ad_dumu2), .load(demultiplexer_1_out3), .in(in), .out(ram512_4_out));
  RAM512 ram512_5 (.adress(adress_1), .adress_dumu(ad_dumu2), .load(demultiplexer_1_out4), .in(in), .out(ram512_5_out));
  RAM512 ram512_6 (.adress(adress_1), .adress_dumu(ad_dumu2), .load(demultiplexer_1_out5), .in(in), .out(ram512_6_out));
  RAM512 ram512_7 (.adress(adress_1), .adress_dumu(ad_dumu2), .load(demultiplexer_1_out6), .in(in), .out(ram512_7_out));
  RAM512 ram512_8 (.adress(adress_1), .adress_dumu(ad_dumu2), .load(demultiplexer_1_out7), .in(in), .out(ram512_8_out));
  Multiplexer #(.select(3), .width(16)) multiplexer_1 (
    .in0(ram512_1_out), .in1(ram512_2_out), .in2(ram512_3_out), .in3(ram512_4_out), .in4(ram512_5_out),
    .in5(ram512_6_out), .in6(ram512_7_out), .in7(ram512_8_out), .out(out), .sel(ad_dumu3));  // open: en
endmodule

module RAM16k (
  input  [2:0] address_dumu4,
  input  [2:0] address_dumu3,
  input  [2:0] address_dumu2,
  input  [5:0] address1,
  input  load,
  input  [15:0] in,
  output [15:0] out
);

  wire demultiplexer_1_out0, demultiplexer_1_out1, demultiplexer_1_out2, demultiplexer_1_out3,
       demultiplexer_1_out4, demultiplexer_1_out5, demultiplexer_1_out6, demultiplexer_1_out7;
  wire [15:0] ram4k_1_out, ram4k_2_out, ram4k_3_out, ram4k_4_out, ram4k_5_out, ram4k_6_out, ram4k_7_out,
       ram4k_8_out;

  Clock clock_1 ();  // open: out
  Demultiplexer #(.select(3)) demultiplexer_1 (
    .out0(demultiplexer_1_out0), .out1(demultiplexer_1_out1), .out2(demultiplexer_1_out2),
    .out3(demultiplexer_1_out3), .out4(demultiplexer_1_out4), .out5(demultiplexer_1_out5),
    .out6(demultiplexer_1_out6), .out7(demultiplexer_1_out7), .in(load), .sel(address_dumu4));  // open: en
  RAM4k ram4k_1 (
    .ad_dumu3(address_dumu3), .ad_dumu2(address_dumu2), .adress_1(address1), .load(demultiplexer_1_out0),
    .in(in), .out(ram4k_1_out));
  RAM4k ram4k_2 (
    .ad_dumu3(address_dumu3), .ad_dumu2(address_dumu2), .adress_1(address1), .load(demultiplexer_1_out1),
    .in(in), .out(ram4k_2_out));
  RAM4k ram4k_3 (
    .ad_dumu3(address_dumu3), .ad_dumu2(address_dumu2), .adress_1(address1), .load(demultiplexer_1_out2),
    .in(in), .out(ram4k_3_out));
  RAM4k ram4k_4 (
    .ad_dumu3(address_dumu3), .ad_dumu2(address_dumu2), .adress_1(address1), .load(demultiplexer_1_out3),
    .in(in), .out(ram4k_4_out));
  RAM4k ram4k_5 (
    .ad_dumu3(address_dumu3), .ad_dumu2(address_dumu2), .adress_1(address1), .load(demultiplexer_1_out4),
    .in(in), .out(ram4k_5_out));
  RAM4k ram4k_6 (
    .ad_dumu3(address_dumu3), .ad_dumu2(address_dumu2), .adress_1(address1), .load(demultiplexer_1_out5),
    .in(in), .out(ram4k_6_out));
  RAM4k ram4k_7 (
    .ad_dumu3(address_dumu3), .ad_dumu2(address_dumu2), .adress_1(address1), .load(demultiplexer_1_out6),
    .in(in), .out(ram4k_7_out));
  RAM4k ram4k_8 (
    .ad_dumu3(address_dumu3), .ad_dumu2(address_dumu2), .adress_1(address1), .load(demultiplexer_1_out7),
    .in(in), .out(ram4k_8_out));
  Multiplexer #(.select(3), .width(16)) multiplexer_1 (
    .in0(ram4k_1_out), .in1(ram4k_2_out), .in2(ram4k_3_out), .in3(ram4k_4_out), .in4(ram4k_5_out),
    .in5(ram4k_6_out), .in6(ram4k_7_out), .in7(ram4k_8_out), .out(out), .sel(address_dumu4));  // open: en
endmodule
